# Fritzing sketch NFCYoklama Şema (saved by Fritzing 0.9.10b)
stripboards: 1

parts:
  T3_Vakfı1 = Generic shrouded header - 32 pins [package=THT]
  DENEYAP_KART1 = DENEYAP OLED EKRAN [package="DIP (Dual Inline) [THT]"]  # not connected
  Parça1 = RFID-RC522-v3
  J1 = Piezo Speaker

nets:
  N1: T3_Vakfı1.pin1, T3_Vakfı1.pin32, Parça1.GND, J1.pin1
  N2: T3_Vakfı1.pin2, T3_Vakfı1.pin31, Parça1.RST
  N3: T3_Vakfı1.pin3, T3_Vakfı1.pin30
  N4: T3_Vakfı1.pin4, T3_Vakfı1.pin29
  N5: T3_Vakfı1.pin5, T3_Vakfı1.pin28
  N6: T3_Vakfı1.pin6, T3_Vakfı1.pin27
  N7: T3_Vakfı1.pin7, T3_Vakfı1.pin26, Parça1.SCK
  N8: T3_Vakfı1.pin8, T3_Vakfı1.pin25, Parça1.MISO
  N9: T3_Vakfı1.pin9, T3_Vakfı1.pin24, Parça1.MOSI
  N10: T3_Vakfı1.pin10, T3_Vakfı1.pin23, J1.pin2
  N11: T3_Vakfı1.pin11, T3_Vakfı1.pin22
  N12: T3_Vakfı1.pin12, T3_Vakfı1.pin21, Parça1.SDA
  N13: T3_Vakfı1.pin13, T3_Vakfı1.pin20
  N14: T3_Vakfı1.pin14, T3_Vakfı1.pin19
  N15: T3_Vakfı1.pin15, T3_Vakfı1.pin18, Parça1.3.3V
  N16: T3_Vakfı1.pin16, T3_Vakfı1.pin17

custom parts:
  Generic shrouded header - 32 pins: Ülkemizin mühendislik kaynakları kullanılarak geliştirilen Deneyap Kart; güçlü işlemcisi, dayanıklı tasarımı ve çok yönlü giriş/çıkış pinleri ile kullanıcılara Elektronik Programlama, Nesnelerin İnterneti (IoT) ve Yapay Zeka alanlarında başlangıç seviyesinden endüstriyel uygulamalara kadar her seviyede projeyi yapma imkanı sunuyor.
  DENEYAP OLED EKRAN: https://deneyapkart.org/
  RFID-RC522-v3: A simple China made RFID-RC522 Reader (6x4 cm); do check the pin labels, as this is a MFRC522 based clone.
